# Fritzing sketch cajaFuerte (saved by Fritzing 0.9.9b)

parts:
  LCM1602_IIC1 = LCM1602 IIC [part_number="LCM1602 IIC" chip_label="LCM1602 IIC" package="DIP (Dual Inline) [THT]"]
  Arduino_UNO = Arduino Uno (Rev3)
  R1 = Resistor [tolerance=±10% power=0.25 resistance=330 package=THT]
  LED1 = LED - 3mm [color="Red (633nm)" current=0.030 package="3 mm [THT]"]
  LED2 = LED - 3mm [color="Green (555nm)" current=0.030 package="3 mm [THT]"]
  R2 = Resistor [tolerance=±10% power=0.25 resistance=330 package=THT]
  LCD+I2C = LCD-16X2 [package=lcd-16x2]
  M1 = Dagu DGServo 9g (Top view) [part_number=RS001B]
  POWER_BANK_USB = USB+SHIELD [package=usb-b-pth]
  VCC1 = Battery
  Teclado = KEYPAD 4x4

nets:
  VSS: LCM1602_IIC1.VSS, LCD+I2C.VSS
  VDD: LCM1602_IIC1.VDD, LCD+I2C.VDD
  N1: LCM1602_IIC1.V0, LCD+I2C.VO
  N2: LCM1602_IIC1.RS, LCD+I2C.RS
  N3: LCM1602_IIC1.RW, LCD+I2C.R_W
  N4: LCM1602_IIC1.E, LCD+I2C.E
  N5: LCM1602_IIC1.D0, LCD+I2C.DB0
  N6: LCM1602_IIC1.D1, LCD+I2C.DB1
  N7: LCM1602_IIC1.D2, LCD+I2C.DB2
  N8: LCM1602_IIC1.D3, LCD+I2C.DB3
  N9: LCM1602_IIC1.D4, LCD+I2C.DB4
  N10: LCM1602_IIC1.D5, LCD+I2C.DB5
  N11: LCM1602_IIC1.D6, LCD+I2C.DB6
  N12: LCM1602_IIC1.D7, LCD+I2C.DB7
  N13: LCM1602_IIC1.A, LCD+I2C.A
  N14: LCM1602_IIC1.K, LCD+I2C.K
  GND: LCM1602_IIC1.GND, Arduino_UNO.GND, LED1.cathode, LED2.cathode, M1.gnd, POWER_BANK_USB.GND, VCC1.-
  5V: LCM1602_IIC1.VCC, Arduino_UNO.5V, M1.vcc, POWER_BANK_USB.VBUS, VCC1.+
  N15: LCM1602_IIC1.SDA, Arduino_UNO.A4/SDA
  N16: LCM1602_IIC1.SCL, Arduino_UNO.A5/SCL
  N17: LCM1602_IIC1.LED_A, LCM1602_IIC1.LED_B
  N18: Arduino_UNO.D8, Teclado.row2
  N19: Arduino_UNO.D9_PWM, Teclado.row1
  N20: Arduino_UNO.D10_PWM/SS, M1.pulse
  N21: Arduino_UNO.D11_PWM/MOSI, R2.Pin_0
  N22: Arduino_UNO.D12/MISO, R1.Pin_0
  N23: Arduino_UNO.D2, Teclado.col4
  N24: Arduino_UNO.D3_PWM, Teclado.col3
  N25: Arduino_UNO.D4, Teclado.col2
  N26: Arduino_UNO.D5_PWM, Teclado.col1
  N27: Arduino_UNO.D6_PWM, Teclado.row4
  N28: Arduino_UNO.D7, Teclado.row3
  N29: R1.Pin_1, LED2.anode
  N30: LED1.anode, R2.Pin_1

notes:
  POWER BANK 5V - USB
  SERVO
  LCD + I2C
  TECLADO

custom parts:
  LCM1602 IIC: I2C-Module to use a 1602 or 2004 LCD on with the wire.h libory Serial LCD Modul
  Battery: Your standard 2x 18650 battery pack (7,4 Volts)
  KEYPAD 4x4: Matrix keypad 16 buttons, 4 rows x 4 columns
